// Logisim project e2448488.circ as structural Verilog: 1 circuit, main circuit main
module main (
  input  O2,
  input  O1,
  input  O0,
  input  A1,
  input  B1,
  input  A0,
  input  B0,
  input  in_8,
  output L0,
  output L1,
  output L2,
  output L3,
  output L4,
  output L5,
  output L6,
  output S
);

  wire and_1_out, and_2_out, n3_to_8_decoder_74138_1_p8, n3_to_8_decoder_74138_1_p9,
       n3_to_8_decoder_74138_1_p10, n3_to_8_decoder_74138_1_p11, n3_to_8_decoder_74138_1_p12,
       n3_to_8_decoder_74138_1_p13, n3_to_8_decoder_74138_1_p14, n3_to_8_decoder_74138_2_p1,
       n3_to_8_decoder_74138_2_p3, n3_to_8_decoder_74138_5_p1, n3_to_8_decoder_74138_5_p2,
       n3_to_8_decoder_74138_6_p7, n3_to_8_decoder_74138_7_p4, n3_to_8_decoder_74138_8_p1,
       n3_to_8_decoder_74138_8_p8, n3_to_8_decoder_74138_8_p9, n3_to_8_decoder_74138_9_p10,
       n3_to_8_decoder_74138_9_p11, n3_to_8_decoder_74138_9_p12, n3_to_8_decoder_74138_9_p13,
       n4_to_1_mux_x2_74153_1_p12, n4_to_1_mux_x2_74153_1_p13, n4_to_1_mux_x2_74153_1_p14,
       n4_to_1_mux_x2_74153_2_p1, n4_to_1_mux_x2_74153_2_p2, n4_to_1_mux_x2_74153_2_p9,
       n4_to_1_mux_x2_74153_3_p3, n4_to_1_mux_x2_74153_3_p4, n4_to_1_mux_x2_74153_3_p5,
       n4_to_1_mux_x2_74153_3_p10, n4_to_1_mux_x2_74153_4_p13, n4_to_1_mux_x2_74153_5_p13,
       n4_to_1_mux_x2_74153_6_p2, n4_to_1_mux_x2_74153_6_p4, n4_to_1_mux_x2_74153_6_p9,
       n4_to_1_mux_x2_74153_6_p10, n4_to_1_mux_x2_74153_7_p12, nor_1_out, nor_2_out, not_1_out, not_4_out,
       not_5_out, not_6_out, not_7_out, not_8_out, not_9_out, not_10_out, not_11_out, not_12_out, not_13_out,
       not_14_out, not_15_out, not_16_out, not_18_out, not_19_out, not_20_out, not_21_out, not_22_out,
       not_26_out, not_27_out, not_28_out, not_29_out, not_31_out, not_32_out, not_34_out, not_35_out,
       not_36_out, not_37_out, not_42_out, not_43_out, not_44_out, not_45_out, not_46_out, not_48_out,
       or_1_out, or_2_out, or_3_out, or_4_out, or_5_out, or_6_out, or_7_out, or_8_out, or_9_out, or_10_out,
       or_11_out, or_12_out, or_14_out, or_16_out, or_17_out, or_18_out, or_19_out, or_20_out, or_21_out,
       or_22_out, or_23_out, or_24_out, or_25_out;

  // _3_to_8_decoder__74138 #(.Facing("east")) 3_to_8_decoder_74138_1: pin names not known; wires that end beside it: 1'b1, O0, O1, O2, 1'b1, in_8, in_8, n3_to_8_decoder_74138_1_p8, n3_to_8_decoder_74138_1_p9, n3_to_8_decoder_74138_1_p10, n3_to_8_decoder_74138_1_p11, n3_to_8_decoder_74138_1_p12, n3_to_8_decoder_74138_1_p13, n3_to_8_decoder_74138_1_p14
  and and_1 (and_1_out, B1, A1);
  and and_2 (and_2_out, A0, B0);
  nor nor_1 (nor_1_out, B1, A1);
  nor nor_2 (nor_2_out, A0, B0);
  not not_1 (not_1_out, A1);
  // _4_to_1_MUX__x2___74153 #(.Facing("east")) 4_to_1_mux_x2_74153_1: pin names not known; wires that end beside it: A1, not_1_out, not_1_out, A1, 1'b0, A1, A1, 1'b1, 1'b0, B1, 1'b0, n4_to_1_mux_x2_74153_1_p12, n4_to_1_mux_x2_74153_1_p13, n4_to_1_mux_x2_74153_1_p14
  // _4_to_1_MUX__x2___74153 #(.Facing("east")) 4_to_1_mux_x2_74153_2: pin names not known; wires that end beside it: n4_to_1_mux_x2_74153_2_p1, n4_to_1_mux_x2_74153_2_p2, n4_to_1_mux_x2_74153_2_p2, n4_to_1_mux_x2_74153_2_p1, n4_to_1_mux_x2_74153_2_p1, 1'b1, n3_to_8_decoder_74138_1_p9, n3_to_8_decoder_74138_1_p9, n4_to_1_mux_x2_74153_2_p9, S
  not not_2 (n4_to_1_mux_x2_74153_2_p2, n4_to_1_mux_x2_74153_2_p1);
  // _4_to_1_MUX__x2___74153 #(.Facing("east")) 4_to_1_mux_x2_74153_3: pin names not known; wires that end beside it: 1'b0, n4_to_1_mux_x2_74153_2_p1, n4_to_1_mux_x2_74153_3_p3, n4_to_1_mux_x2_74153_3_p4, n4_to_1_mux_x2_74153_3_p5, 1'b1, A1, n3_to_8_decoder_74138_1_p11, B1, n4_to_1_mux_x2_74153_3_p10
  nor nor_3 (n4_to_1_mux_x2_74153_3_p3, A1, A0);
  not not_3 (n4_to_1_mux_x2_74153_3_p4, A1);
  nand nand_1 (n4_to_1_mux_x2_74153_3_p5, A1, A0);
  // _3_to_8_decoder__74138 #(.Facing("east")) 3_to_8_decoder_74138_2: pin names not known; wires that end beside it: n3_to_8_decoder_74138_2_p1, 1'b0, n3_to_8_decoder_74138_2_p3, B0, B1
  xor xor_1 (n3_to_8_decoder_74138_2_p3, B1, A1);
  xor xor_2 (n3_to_8_decoder_74138_2_p1, A0, B0);
  // _3_to_8_decoder__74138 #(.Facing("east")) 3_to_8_decoder_74138_3: pin names not known; wires that end beside it: n3_to_8_decoder_74138_1_p10, and_2_out, and_1_out, 1'b0, 1'b1, n3_to_8_decoder_74138_1_p12, 1'b0
  // _3_to_8_decoder__74138 #(.Facing("east")) 3_to_8_decoder_74138_4: pin names not known; wires that end beside it: nor_2_out, nor_1_out, 1'b0, 1'b1, n3_to_8_decoder_74138_1_p13, 1'b0
  // _3_to_8_decoder__74138 #(.Facing("east")) 3_to_8_decoder_74138_5: pin names not known; wires that end beside it: n3_to_8_decoder_74138_5_p1, n3_to_8_decoder_74138_5_p2, 1'b0, 1'b1, 1'b1, n3_to_8_decoder_74138_1_p14, n3_to_8_decoder_74138_1_p12, 1'b0, 1'b0
  xor xor_3 (n3_to_8_decoder_74138_5_p2, B1, A1);
  xor xor_4 (n3_to_8_decoder_74138_5_p1, A0, B0);
  // NOT_Gate not_4 has open pins: in=open, out=not_4_out
  // NOT_Gate not_5 has open pins: in=open, out=not_5_out
  // NOT_Gate not_6 has open pins: in=open, out=not_6_out
  // NOT_Gate not_7 has open pins: in=open, out=not_7_out
  // NOT_Gate not_8 has open pins: in=open, out=not_8_out
  // NOT_Gate not_9 has open pins: in=open, out=not_9_out
  // NOT_Gate not_10 has open pins: in=open, out=not_10_out
  // NOT_Gate not_11 has open pins: in=open, out=not_11_out
  // NOT_Gate not_12 has open pins: in=open, out=not_12_out
  // NOT_Gate not_13 has open pins: in=open, out=not_13_out
  // NOT_Gate not_14 has open pins: in=open, out=not_14_out
  // NOT_Gate not_15 has open pins: in=open, out=not_15_out
  not not_16 (not_16_out, A0);
  // _4_to_1_MUX__x2___74153 #(.Facing("east")) 4_to_1_mux_x2_74153_4: pin names not known; wires that end beside it: A0, not_16_out, not_16_out, A0, 1'b0, A0, A0, 1'b1, 1'b0, B0, 1'b0, 1'b0, n4_to_1_mux_x2_74153_4_p13, n4_to_1_mux_x2_74153_1_p12
  // _4_to_1_MUX__x2___74153 #(.Facing("east")) 4_to_1_mux_x2_74153_5: pin names not known; wires that end beside it: 1'b0, 1'b1, 1'b1, 1'b0, 1'b0, 1'b1, 1'b0, 1'b0, n3_to_8_decoder_74138_1_p9, A0, n3_to_8_decoder_74138_1_p9, B0, n4_to_1_mux_x2_74153_5_p13, n4_to_1_mux_x2_74153_2_p1
  // _4_to_1_MUX__x2___74153 #(.Facing("east")) 4_to_1_mux_x2_74153_6: pin names not known; wires that end beside it: 1'b0, n4_to_1_mux_x2_74153_6_p2, 1'b0, n4_to_1_mux_x2_74153_6_p4, 1'b0, A0, n3_to_8_decoder_74138_1_p10, n3_to_8_decoder_74138_1_p10, n4_to_1_mux_x2_74153_6_p9, n4_to_1_mux_x2_74153_6_p10
  nor nor_4 (n4_to_1_mux_x2_74153_6_p2, A1, A0);
  not not_17 (n4_to_1_mux_x2_74153_6_p4, A0);
  // _4_to_1_MUX__x2___74153 #(.Facing("east")) 4_to_1_mux_x2_74153_7: pin names not known; wires that end beside it: n4_to_1_mux_x2_74153_6_p4, 1'b1, 1'b0, A1, A0, A0, B0, n3_to_8_decoder_74138_1_p10, B0, B1, B1, n4_to_1_mux_x2_74153_7_p12
  // _3_to_8_decoder__74138 #(.Facing("east")) 3_to_8_decoder_74138_6: pin names not known; wires that end beside it: n4_to_1_mux_x2_74153_4_p13, n4_to_1_mux_x2_74153_1_p13, n4_to_1_mux_x2_74153_1_p14, 1'b1, n3_to_8_decoder_74138_1_p8, 1'b0, n3_to_8_decoder_74138_6_p7
  // _3_to_8_decoder__74138 #(.Facing("east")) 3_to_8_decoder_74138_7: pin names not known; wires that end beside it: n4_to_1_mux_x2_74153_5_p13, n4_to_1_mux_x2_74153_2_p9, S, n3_to_8_decoder_74138_7_p4
  // _3_to_8_decoder__74138 #(.Facing("east")) 3_to_8_decoder_74138_8: pin names not known; wires that end beside it: n3_to_8_decoder_74138_8_p1, n4_to_1_mux_x2_74153_3_p10, 1'b0, 1'b0, 1'b1, n3_to_8_decoder_74138_1_p9, 1'b0, n3_to_8_decoder_74138_8_p8, n3_to_8_decoder_74138_8_p9
  // _3_to_8_decoder__74138 #(.Facing("east")) 3_to_8_decoder_74138_9: pin names not known; wires that end beside it: n4_to_1_mux_x2_74153_6_p9, n4_to_1_mux_x2_74153_6_p10, n4_to_1_mux_x2_74153_7_p12, 1'b1, 1'b1, n3_to_8_decoder_74138_1_p11, n3_to_8_decoder_74138_1_p10, 1'b0, 1'b0, n3_to_8_decoder_74138_9_p10, n3_to_8_decoder_74138_9_p11, n3_to_8_decoder_74138_9_p12, n3_to_8_decoder_74138_9_p13
  // NOT_Gate not_18 has open pins: in=open, out=not_18_out
  // NOT_Gate not_19 has open pins: in=open, out=not_19_out
  // NOT_Gate not_20 has open pins: in=open, out=not_20_out
  // NOT_Gate not_21 has open pins: in=open, out=not_21_out
  // NOT_Gate not_22 has open pins: in=open, out=not_22_out
  // NOT_Gate not_23 has open pins: in=open, out=L5
  // NOT_Gate not_24 has open pins: in=open, out=n3_to_8_decoder_74138_6_p7
  // NOT_Gate not_25 is placed but not wired
  // NOT_Gate not_26 has open pins: in=open, out=not_26_out
  // NOT_Gate not_27 has open pins: in=open, out=not_27_out
  // NOT_Gate not_28 has open pins: in=open, out=not_28_out
  // NOT_Gate not_29 has open pins: in=open, out=not_29_out
  // NOT_Gate not_30 has open pins: in=open, out=n3_to_8_decoder_74138_7_p4
  // NOT_Gate not_31 has open pins: in=open, out=not_31_out
  // NOT_Gate not_32 has open pins: in=open, out=not_32_out
  // NOT_Gate not_33 has open pins: in=open, out=n3_to_8_decoder_74138_8_p1
  // NOT_Gate not_34 has open pins: in=open, out=not_34_out
  // NOT_Gate not_35 has open pins: in=open, out=not_35_out
  // NOT_Gate not_36 has open pins: in=open, out=not_36_out
  // NOT_Gate not_37 has open pins: in=open, out=not_37_out
  // NOT_Gate not_38 has open pins: in=open, out=n3_to_8_decoder_74138_8_p8
  // NOT_Gate not_39 has open pins: in=open, out=n3_to_8_decoder_74138_8_p9
  // NOT_Gate not_40 has open pins: in=open, out=n3_to_8_decoder_74138_9_p10
  // NOT_Gate not_41 has open pins: in=open, out=n3_to_8_decoder_74138_9_p11
  // NOT_Gate not_42 has open pins: in=open, out=not_42_out
  // NOT_Gate not_43 has open pins: in=open, out=not_43_out
  // NOT_Gate not_44 has open pins: in=open, out=not_44_out
  // NOT_Gate not_45 has open pins: in=open, out=not_45_out
  // NOT_Gate not_46 has open pins: in=open, out=not_46_out
  // NOT_Gate not_47 has open pins: in=open, out=n3_to_8_decoder_74138_9_p12
  // NOT_Gate not_48 has open pins: in=open, out=not_48_out
  // NOT_Gate not_49 has open pins: in=open, out=n3_to_8_decoder_74138_9_p13
  or or_1 (or_1_out, not_18_out, not_26_out);
  or or_2 (or_2_out, not_34_out, not_42_out);
  or or_3 (or_3_out, not_4_out, not_8_out);
  or or_4 (or_4_out, not_19_out, not_27_out);
  or or_5 (or_5_out, not_35_out, not_43_out);
  or or_6 (or_6_out, not_5_out, not_9_out);
  or or_7 (or_7_out, not_20_out, not_28_out);
  or or_8 (or_8_out, not_36_out, not_44_out);
  or or_9 (or_9_out, not_6_out, not_10_out);
  or or_10 (or_10_out, not_21_out, not_31_out);
  or or_11 (or_11_out, not_45_out, not_7_out);
  or or_12 (or_12_out, not_11_out, not_15_out);
  or or_13 (L4, not_22_out, not_46_out);
  or or_14 (or_14_out, or_1_out, or_2_out);
  or or_15 (L0, or_14_out, or_16_out);
  or or_16 (or_16_out, or_3_out, not_12_out);
  or or_17 (or_17_out, or_4_out, or_5_out);
  or or_18 (or_18_out, or_17_out, or_19_out);
  or or_19 (or_19_out, or_6_out, not_13_out);
  or or_20 (or_20_out, or_7_out, or_8_out);
  or or_21 (or_21_out, or_20_out, or_22_out);
  or or_22 (or_22_out, or_9_out, not_14_out);
  or or_23 (or_23_out, or_10_out, or_11_out);
  or or_24 (or_24_out, or_23_out, or_25_out);
  or or_25 (or_25_out, or_12_out, not_29_out);
  or or_26 (L6, not_48_out, n3_to_8_decoder_74138_6_p7);
  or or_27 (L1, n3_to_8_decoder_74138_8_p1, or_18_out);
  or or_28 (L2, not_32_out, or_21_out);
  or or_29 (L3, not_37_out, or_24_out);

  // Notes on the sheet:
  //   greater equal
  //   xor
  //   xor
  //   xor
  //   adder
  //   subtractor
endmodule
